# Fritzing sketch cableado (saved by Fritzing 0.9.9b)
breadboards: 1

parts:
  Componente1 = Arduino Nano (Rev3.0)
  PCB2 = RTC_DS1302_module
  Componente2 = Matrix LED de 8x8 basada en MAX7219
  Componente3 = Matrix LED de 8x8 basada en MAX7219
  Componente5 = Matrix LED de 8x8 basada en MAX7219
  Componente4 = Matrix LED de 8x8 basada en MAX7219

nets:
  GND: Componente1.GND, PCB2.GND, Componente2.GND#1
  N1: Componente1.D4, Componente2.DIN
  N2: Componente1.D5, Componente2.CLK
  N3: Componente1.D6, Componente2.CS
  N4: Componente1.D10, PCB2.CLK
  N5: Componente1.D11/MOSI, PCB2.DAT
  N6: Componente1.D12/MISO, PCB2.RST
  VCC: Componente1.VIN, PCB2.VCC, Componente2.VCC
  N7: Componente2.VCC(OUT), Componente3.VCC
  N8: Componente2.GND#6, Componente3.GND#1
  N9: Componente2.CS(OUT), Componente3.CS
  N10: Componente2.CLK(OUT), Componente3.CLK
  N11: Componente2.DOUT, Componente3.DIN
  N12: Componente3.VCC(OUT), Componente4.VCC
  N13: Componente3.GND#6, Componente4.GND#1
  N14: Componente3.CS(OUT), Componente4.CS
  N15: Componente3.CLK(OUT), Componente4.CLK
  N16: Componente3.DOUT, Componente4.DIN
  N17: Componente5.VCC, Componente4.VCC(OUT)
  N18: Componente5.GND, Componente4.GND#6
  N19: Componente5.CS, Componente4.CS(OUT)
  N20: Componente5.CLK, Componente4.CLK(OUT)
  N21: Componente5.DIN, Componente4.DOUT

custom parts:
  RTC_DS1302_module: Arduino module DS1302 SPI Real Time Clock
